# Fritzing sketch DR5000DR4088Track3 (saved by Fritzing 0.9.3b)

parts:
  Track1 = Track3
  DR1 = DR4088
  DR2 = DR5000
  D1 = Diode [package=diode-1n4148]
  D3 = Diode [package=diode-1n4148]
  D4 = Diode [package=diode-1n4148]
  D5 = Diode [package=diode-1n4001]
  R1 = Resistor [tolerance=±5% resistance=4.7k package=THT]

nets:
  N1: Track1.LEFT, Track1.RIGHT, DR1.1, DR1.2
  N2: Track1.MIDDLE, D1.C, D3.A, R1.Pin_0
  N3: Track1.COMMON, DR2.TRACKOUTPUT#5
  N4: DR1.COMMON, DR2.TRACKOUTPUT#4, D4.C, D5.A, R1.Pin_1
  N5: DR1.LOCONET, DR2.LocoNetT
  N6: D1.A, D5.C
  N7: D3.C, D4.A
