# Fritzing sketch DCCNextschematicTester (saved by Fritzing 0.9.3b)

parts:
  Module1 = DCCNext
  LED33 = LED - 5mm [color="Green (570nm)" package="5 mm [THT]"]
  LED35 = LED - 5mm [color="Yellow (595nm)" package="5 mm [THT]"]
  LED36 = LED - 5mm [color="Red (633nm)" package="5 mm [THT]"]
  LED37 = LED - 5mm [color="Green (570nm)" package="5 mm [THT]"]
  LED38 = LED - 5mm [color="White (4500K)" package="5 mm [THT]"]
  LED39 = LED - 5mm [color="Yellow (595nm)" package="5 mm [THT]"]
  LED40 = LED - 5mm [color="Red (633nm)" package="5 mm [THT]"]
  LED41 = LED - 5mm [color="White (4500K)" package="5 mm [THT]"]
  LED42 = LED - 5mm [color="Green (570nm)" package="5 mm [THT]"]
  LED43 = LED - 5mm [color="Yellow (595nm)" package="5 mm [THT]"]
  LED44 = LED - 5mm [color="Red (633nm)" package="5 mm [THT]"]
  LED45 = LED - 5mm [color="White (4500K)" package="5 mm [THT]"]
  LED46 = LED - 5mm [color="Green (570nm)" package="5 mm [THT]"]
  LED47 = LED - 5mm [color="Yellow (595nm)" package="5 mm [THT]"]
  LED48 = LED - 5mm [color="White (4500K)" package="5 mm [THT]"]
  R33 = Resistor [tolerance=±1% resistance=1.5k package=THT]
  R34 = Resistor [tolerance=±1% resistance=1.5k package=THT]
  R35 = Resistor [tolerance=±1% resistance=1.5k package=THT]
  R36 = Resistor [tolerance=±1% resistance=1.5k package=THT]
  R37 = Resistor [tolerance=±1% resistance=1.5k package=THT]
  R38 = Resistor [tolerance=±1% resistance=1.5k package=THT]
  R39 = Resistor [tolerance=±1% resistance=1.5k package=THT]
  R40 = Resistor [tolerance=±1% resistance=1.5k package=THT]
  R41 = Resistor [tolerance=±1% resistance=1.5k package=THT]
  R42 = Resistor [tolerance=±1% resistance=1.5k package=THT]
  R43 = Resistor [tolerance=±1% resistance=1.5k package=THT]
  R44 = Resistor [tolerance=±1% resistance=1.5k package=THT]
  R45 = Resistor [tolerance=±1% resistance=1.5k package=THT]
  R46 = Resistor [tolerance=±1% resistance=1.5k package=THT]
  R47 = Resistor [tolerance=±1% resistance=1.5k package=THT]
  LED34 = smd LED [color="White (4500K)" package="0603 [SMD]"]
  LED34_2 = smd LED [color="Red (660nm)" package="0603 [SMD]"]
  R48 = Resistor [tolerance=±1% resistance=1.5k package=THT]

nets:
  N1: Module1.1, R35.Pin_1
  N2: Module1.2, R36.Pin_1
  N3: Module1.3, R33.Pin_1
  N4: Module1.4, R39.Pin_1
  N5: Module1.5, R34.Pin_1
  N6: Module1.6, R40.Pin_1
  N7: Module1.7, R37.Pin_1
  N8: Module1.8, R42.Pin_1
  N9: Module1.9, R38.Pin_1
  N10: Module1.10, R43.Pin_1
  N11: Module1.11, R44.Pin_1
  N12: Module1.12, R45.Pin_1
  N13: Module1.13, R41.Pin_1
  N14: Module1.14, R47.Pin_1
  N15: Module1.15, R46.Pin_1
  N16: Module1.16, R48.Pin_1
  N17: Module1.+5V, LED33.anode, LED35.anode, LED36.anode, LED37.anode, LED38.anode, LED39.anode, LED40.anode, LED41.anode, LED42.anode, LED43.anode, LED44.anode, LED45.anode, LED46.anode, LED47.anode, LED48.anode, LED34_2.anode
  N18: LED33.cathode, R33.Pin_0
  N19: LED35.cathode, R36.Pin_0
  N20: LED36.cathode, R34.Pin_0
  N21: LED37.cathode, R37.Pin_0
  N22: LED38.cathode, R39.Pin_0
  N23: LED39.cathode, R40.Pin_0
  N24: LED40.cathode, R38.Pin_0
  N25: LED41.cathode, R42.Pin_0
  N26: LED42.cathode, R44.Pin_0
  N27: LED43.cathode, R43.Pin_0
  N28: LED44.cathode, R41.Pin_0
  N29: LED45.cathode, R45.Pin_0
  N30: LED46.cathode, R46.Pin_0
  N31: LED47.cathode, R47.Pin_0
  N32: LED48.cathode, R48.Pin_0
  N33: R35.Pin_0, LED34.cathode, LED34_2.cathode
