# Fritzing sketch DR4018_2_switches_4_NS3light (saved by Fritzing 0.9.3b)

parts:
  Onderdeel1 = DR4018
  Switch1 = Switch
  Switch2 = Switch
  Sein1 = Sein3
  Sein2 = Sein3
  Sein3 = Sein3
  Sein4 = Sein3

nets:
  N1: Onderdeel1.1, Onderdeel1.C#15, Switch1.STRAIGHT, Switch1.COMMON
  N2: Onderdeel1.2, Switch1.THROWN
  N3: Onderdeel1.3, Onderdeel1.C#18, Onderdeel1.4, Onderdeel1.5, Onderdeel1.7, Onderdeel1.8, Onderdeel1.10, Switch2.STRAIGHT, Switch2.THROWN, Switch2.COMMON, Sein1.RED, Sein1.GREEN, Sein2.RED, Sein2.GREEN
  N4: Onderdeel1.C#21, Sein1.COMMON
  N5: Onderdeel1.6, Sein1.YELLOW
  N6: Onderdeel1.9, Sein2.YELLOW
  N7: Onderdeel1.C#30, Sein2.COMMON
  N8: Onderdeel1.11, Onderdeel1.13, Sein3.RED, Sein3.GREEN
  N9: Onderdeel1.C#33, Sein3.COMMON
  N10: Onderdeel1.12, Sein3.YELLOW
  N11: Onderdeel1.14, Onderdeel1.16, Sein4.RED, Sein4.GREEN
  N12: Onderdeel1.15, Sein4.YELLOW
  N13: Onderdeel1.C#39, Sein4.COMMON
