# Fritzing sketch DR4018_4_sein4 (saved by Fritzing 0.9.3b)

parts:
  Sein1 = Sein4
  Onderdeel1 = DR4018
  Sein2 = Sein4
  Sein3 = Sein4
  Sein4 = Sein4

nets:
  N1: Sein1.RED, Sein1.GREEN, Onderdeel1.1, Onderdeel1.3, Onderdeel1.8, Sein2.WHITE
  N2: Sein1.YELLOW, Onderdeel1.2
  N3: Sein1.WHITE, Onderdeel1.4, Onderdeel1.5, Onderdeel1.7, Sein2.RED, Sein2.GREEN
  N4: Sein1.COMMON, Onderdeel1.C#15
  N5: Onderdeel1.C#21, Sein2.COMMON
  N6: Onderdeel1.6, Sein2.YELLOW
  N7: Onderdeel1.9, Onderdeel1.11, Sein3.RED, Sein3.GREEN
  N8: Onderdeel1.C#30, Sein3.COMMON
  N9: Onderdeel1.10, Sein3.YELLOW
  N10: Onderdeel1.12, Sein3.WHITE
  N11: Onderdeel1.13, Onderdeel1.15, Sein4.RED, Sein4.GREEN
  N12: Onderdeel1.C#36, Sein4.COMMON
  N13: Onderdeel1.14, Sein4.YELLOW
  N14: Onderdeel1.16, Sein4.WHITE
