# Fritzing sketch DR4018_5_sein3 (saved by Fritzing 0.9.3b)

parts:
  Onderdeel1 = DR4018
  Sein6 = Sein3
  Sein7 = Sein3
  Sein8 = Sein3
  Sein9 = Sein3
  Sein10 = Sein3

nets:
  N1: Onderdeel1.1, Onderdeel1.3, Onderdeel1.8, Sein6.RED, Sein6.GREEN, Sein8.YELLOW
  N2: Onderdeel1.C#15, Sein6.COMMON
  N3: Onderdeel1.2, Sein6.YELLOW
  N4: Onderdeel1.4, Onderdeel1.6, Onderdeel1.7, Onderdeel1.9, Sein7.RED, Sein7.GREEN, Sein8.RED, Sein8.GREEN
  N5: Onderdeel1.5, Sein7.YELLOW
  N6: Onderdeel1.C#21, Sein7.COMMON
  N7: Onderdeel1.C#27, Sein8.COMMON
  N8: Onderdeel1.10, Onderdeel1.12, Sein9.RED, Sein9.GREEN
  N9: Onderdeel1.11, Sein9.YELLOW
  N10: Onderdeel1.C#33, Sein9.COMMON
  N11: Onderdeel1.13, Onderdeel1.15, Sein10.RED, Sein10.GREEN
  N12: Onderdeel1.C#36, Sein10.COMMON
  N13: Onderdeel1.14, Sein10.YELLOW
