# Fritzing sketch DR4018_8_sein2 (saved by Fritzing 0.9.3b)

parts:
  Onderdeel1 = DR4018
  Signal1 = Signal2
  Signal2 = Signal2
  Signal3 = Signal2
  Signal4 = Signal2
  Signal5 = Signal2
  Signal6 = Signal2
  Signal7 = Signal2
  Signal8 = Signal2

nets:
  N1: Onderdeel1.1, Onderdeel1.C#15, Signal1.RED, Signal1.COMMON
  N2: Onderdeel1.2, Signal1.GREEN
  N3: Onderdeel1.3, Onderdeel1.C#18, Onderdeel1.4, Onderdeel1.7, Onderdeel1.C#27, Onderdeel1.8, Signal2.RED, Signal2.GREEN, Signal2.COMMON, Signal4.RED, Signal4.GREEN, Signal4.COMMON
  N4: Onderdeel1.5, Onderdeel1.C#21, Signal3.RED, Signal3.COMMON
  N5: Onderdeel1.6, Signal3.GREEN
  N6: Onderdeel1.9, Onderdeel1.C#30, Signal5.RED, Signal5.COMMON
  N7: Onderdeel1.10, Signal5.GREEN
  N8: Onderdeel1.11, Onderdeel1.C#33, Signal6.RED, Signal6.COMMON
  N9: Onderdeel1.12, Signal6.GREEN
  N10: Onderdeel1.13, Onderdeel1.C#36, Signal7.RED, Signal7.COMMON
  N11: Onderdeel1.14, Signal7.GREEN
  N12: Onderdeel1.15, Onderdeel1.C#39, Signal8.RED, Signal8.COMMON
  N13: Onderdeel1.16, Signal8.GREEN
