# Fritzing sketch DR4018_8_switches (saved by Fritzing 0.9.3b)

parts:
  Onderdeel1 = DR4018
  Switch1 = Switch
  Switch2 = Switch
  Switch3 = Switch
  Switch4 = Switch
  Switch5 = Switch
  Switch6 = Switch
  Switch7 = Switch
  Switch8 = Switch

nets:
  N1: Onderdeel1.1, Onderdeel1.C#15, Switch1.STRAIGHT, Switch1.COMMON
  N2: Onderdeel1.2, Switch1.THROWN
  N3: Onderdeel1.3, Onderdeel1.C#18, Onderdeel1.4, Onderdeel1.7, Onderdeel1.C#27, Onderdeel1.8, Switch2.STRAIGHT, Switch2.THROWN, Switch2.COMMON, Switch4.STRAIGHT, Switch4.THROWN, Switch4.COMMON
  N4: Onderdeel1.5, Onderdeel1.C#21, Switch3.STRAIGHT, Switch3.COMMON
  N5: Onderdeel1.6, Switch3.THROWN
  N6: Onderdeel1.9, Onderdeel1.C#30, Switch5.STRAIGHT, Switch5.COMMON
  N7: Onderdeel1.10, Switch5.THROWN
  N8: Onderdeel1.11, Onderdeel1.C#33, Switch6.STRAIGHT, Switch6.COMMON
  N9: Onderdeel1.12, Switch6.THROWN
  N10: Onderdeel1.13, Onderdeel1.C#36, Switch7.STRAIGHT, Switch7.COMMON
  N11: Onderdeel1.14, Switch7.THROWN
  N12: Onderdeel1.15, Onderdeel1.C#39, Switch8.STRAIGHT, Switch8.COMMON
  N13: Onderdeel1.16, Switch8.THROWN
