# Fritzing sketch DR4018testerbyhand (saved by Fritzing 0.9.3b)

parts:
  Onderdeel1 = DR4018
  LED17 = LED - 5mm [color="Green (570nm)" package="5 mm [THT]"]
  LED18 = LED - 5mm [color="White (4500K)" package="5 mm [THT]"]
  LED19 = LED - 5mm [color="Yellow (595nm)" package="5 mm [THT]"]
  LED20 = LED - 5mm [color="Red (633nm)" package="5 mm [THT]"]
  LED21 = LED - 5mm [color="Green (570nm)" package="5 mm [THT]"]
  LED22 = LED - 5mm [color="White (4500K)" package="5 mm [THT]"]
  LED23 = LED - 5mm [color="Yellow (595nm)" package="5 mm [THT]"]
  LED24 = LED - 5mm [color="Red (633nm)" package="5 mm [THT]"]
  LED25 = LED - 5mm [color="White (4500K)" package="5 mm [THT]"]
  LED26 = LED - 5mm [color="Green (570nm)" package="5 mm [THT]"]
  LED27 = LED - 5mm [color="Yellow (595nm)" package="5 mm [THT]"]
  LED28 = LED - 5mm [color="Red (633nm)" package="5 mm [THT]"]
  LED29 = LED - 5mm [color="White (4500K)" package="5 mm [THT]"]
  LED30 = LED - 5mm [color="Green (570nm)" package="5 mm [THT]"]
  LED31 = LED - 5mm [color="Yellow (595nm)" package="5 mm [THT]"]
  LED32 = LED - 5mm [color="Red (633nm)" package="5 mm [THT]"]
  R17 = Resistor [tolerance=±1% resistance=1.5k package=THT]
  R18 = Resistor [tolerance=±1% resistance=1.5k package=THT]
  R19 = Resistor [tolerance=±1% resistance=1.5k package=THT]
  R20 = Resistor [tolerance=±1% resistance=1.5k package=THT]
  R21 = Resistor [tolerance=±1% resistance=1.5k package=THT]
  R22 = Resistor [tolerance=±1% resistance=1.5k package=THT]
  R23 = Resistor [tolerance=±1% resistance=1.5k package=THT]
  R24 = Resistor [tolerance=±1% resistance=1.5k package=THT]
  R25 = Resistor [tolerance=±1% resistance=1.5k package=THT]
  R26 = Resistor [tolerance=±1% resistance=1.5k package=THT]
  R27 = Resistor [tolerance=±1% resistance=1.5k package=THT]
  R28 = Resistor [tolerance=±1% resistance=1.5k package=THT]
  R29 = Resistor [tolerance=±1% resistance=1.5k package=THT]
  R30 = Resistor [tolerance=±1% resistance=1.5k package=THT]
  R31 = Resistor [tolerance=±1% resistance=1.5k package=THT]
  R32 = Resistor [tolerance=±1% resistance=1.5k package=THT]

nets:
  N1: Onderdeel1.1, R32.Pin_1
  N2: Onderdeel1.C, LED21.anode, LED23.anode, LED24.anode, LED25.anode, LED26.anode, LED27.anode, LED28.anode, LED29.anode, LED30.anode, LED31.anode, LED32.anode
  N3: Onderdeel1.2, R31.Pin_1
  N4: Onderdeel1.3, Onderdeel1.8, R26.Pin_1, R30.Pin_1
  N5: Onderdeel1.4, Onderdeel1.7, R28.Pin_1, R29.Pin_1
  N6: Onderdeel1.5, R25.Pin_1
  N7: Onderdeel1.6, R27.Pin_1
  N8: Onderdeel1.9, R22.Pin_1
  N9: Onderdeel1.10, R24.Pin_1
  N10: Onderdeel1.11, R21.Pin_1
  N11: Onderdeel1.12, R23.Pin_1
  N12: Onderdeel1.13, R18.Pin_1
  N13: Onderdeel1.14, R20.Pin_1
  N14: Onderdeel1.15, R17.Pin_1
  N15: Onderdeel1.16, R19.Pin_1
  N16: LED17.cathode, R17.Pin_0
  N17: LED17.anode, LED18.anode, LED19.anode, LED20.anode, LED22.anode
  N18: LED18.cathode, R19.Pin_0
  N19: LED19.cathode, R20.Pin_0
  N20: LED20.cathode, R18.Pin_0
  N21: LED21.cathode, R21.Pin_0
  N22: LED22.cathode, R23.Pin_0
  N23: LED23.cathode, R24.Pin_0
  N24: LED24.cathode, R22.Pin_0
  N25: LED25.cathode, R26.Pin_0
  N26: LED26.cathode, R28.Pin_0
  N27: LED27.cathode, R27.Pin_0
  N28: LED28.cathode, R25.Pin_0
  N29: LED29.cathode, R29.Pin_0
  N30: LED30.cathode, R30.Pin_0
  N31: LED31.cathode, R31.Pin_0
  N32: LED32.cathode, R32.Pin_0
