# Fritzing sketch DR4018testerembedded (saved by Fritzing 0.9.3b)

parts:
  Onderdeel2 = DR4018
  LED1 = LED - 5mm [color="Red (633nm)" package="5 mm [THT]"]
  LED2 = LED - 5mm [color="Yellow (595nm)" package="5 mm [THT]"]
  LED3 = LED - 5mm [color="Green (570nm)" package="5 mm [THT]"]
  LED4 = LED - 5mm [color="White (4500K)" package="5 mm [THT]"]
  R1 = Resistor [tolerance=±1% resistance=1.5k package=THT]
  R2 = Resistor [tolerance=±1% resistance=1.5k package=THT]
  R3 = Resistor [tolerance=±1% resistance=1.5k package=THT]
  R4 = Resistor [tolerance=±1% resistance=1.5k package=THT]
  LED5 = LED - 5mm [color="Red (633nm)" package="5 mm [THT]"]
  LED6 = LED - 5mm [color="Yellow (595nm)" package="5 mm [THT]"]
  LED7 = LED - 5mm [color="Green (570nm)" package="5 mm [THT]"]
  LED8 = LED - 5mm [color="White (4500K)" package="5 mm [THT]"]
  R5 = Resistor [tolerance=±1% resistance=1.5k package=THT]
  R6 = Resistor [tolerance=±1% resistance=1.5k package=THT]
  R7 = Resistor [tolerance=±1% resistance=1.5k package=THT]
  R8 = Resistor [tolerance=±1% resistance=1.5k package=THT]
  LED9 = LED - 5mm [color="Red (633nm)" package="5 mm [THT]"]
  LED10 = LED - 5mm [color="Yellow (595nm)" package="5 mm [THT]"]
  LED11 = LED - 5mm [color="White (4500K)" package="5 mm [THT]"]
  LED12 = LED - 5mm [color="Green (570nm)" package="5 mm [THT]"]
  R9 = Resistor [tolerance=±1% resistance=1.5k package=THT]
  R10 = Resistor [tolerance=±1% resistance=1.5k package=THT]
  R11 = Resistor [tolerance=±1% resistance=1.5k package=THT]
  R12 = Resistor [tolerance=±1% resistance=1.5k package=THT]
  LED13 = LED - 5mm [color="Red (633nm)" package="5 mm [THT]"]
  LED14 = LED - 5mm [color="Yellow (595nm)" package="5 mm [THT]"]
  LED15 = LED - 5mm [color="White (4500K)" package="5 mm [THT]"]
  LED16 = LED - 5mm [color="Green (570nm)" package="5 mm [THT]"]
  R13 = Resistor [tolerance=±1% resistance=1.5k package=THT]
  R14 = Resistor [tolerance=±1% resistance=1.5k package=THT]
  R15 = Resistor [tolerance=±1% resistance=1.5k package=THT]
  R16 = Resistor [tolerance=±1% resistance=1.5k package=THT]

nets:
  N1: Onderdeel2.1, R1.Pin_1
  N2: Onderdeel2.C, LED1.anode, LED2.anode, LED3.anode, LED4.anode, LED5.anode, LED6.anode, LED7.anode, LED8.anode, LED9.anode, LED10.anode, LED11.anode, LED12.anode, LED13.anode, LED14.anode, LED15.anode, LED16.anode
  N3: Onderdeel2.2, R2.Pin_1
  N4: Onderdeel2.3, Onderdeel2.8, R3.Pin_1, R7.Pin_1
  N5: Onderdeel2.4, Onderdeel2.7, R4.Pin_1, R5.Pin_1
  N6: Onderdeel2.5, R8.Pin_1
  N7: Onderdeel2.6, R6.Pin_1
  N8: Onderdeel2.9, R11.Pin_1
  N9: Onderdeel2.10, R9.Pin_1
  N10: Onderdeel2.11, R12.Pin_1
  N11: Onderdeel2.12, R10.Pin_1
  N12: Onderdeel2.13, R15.Pin_1
  N13: Onderdeel2.14, R13.Pin_1
  N14: Onderdeel2.15, R16.Pin_1
  N15: Onderdeel2.16, R14.Pin_1
  N16: LED1.cathode, R1.Pin_0
  N17: LED2.cathode, R2.Pin_0
  N18: LED3.cathode, R3.Pin_0
  N19: LED4.cathode, R4.Pin_0
  N20: LED5.cathode, R8.Pin_0
  N21: LED6.cathode, R6.Pin_0
  N22: LED7.cathode, R5.Pin_0
  N23: LED8.cathode, R7.Pin_0
  N24: LED9.cathode, R11.Pin_0
  N25: LED10.cathode, R9.Pin_0
  N26: LED11.cathode, R10.Pin_0
  N27: LED12.cathode, R12.Pin_0
  N28: LED13.cathode, R15.Pin_0
  N29: LED14.cathode, R13.Pin_0
  N30: LED15.cathode, R14.Pin_0
  N31: LED16.cathode, R16.Pin_0
