# Fritzing sketch DR5000DR4018CVReader (saved by Fritzing 0.9.3b)

parts:
  DR1 = DR5000
  Onderdeel1 = DR4018
  R1 = Resistor [tolerance=±5% resistance=220 package=THT]  # not connected

nets:
  N1: DR1.PROGTRACK#10, Onderdeel1.POWER#41, Onderdeel1.SIGNAL#43
  N2: DR1.PROGTRACK#11, Onderdeel1.POWER#42, Onderdeel1.SIGNAL#44
