# Fritzing sketch DR5000DR4088DR4018 (saved by Fritzing 0.9.3b)

parts:
  Track1 = Track3
  DR1 = DR4088
  DR2 = DR5000
  D1 = Diode [package=diode-1n4148]
  D3 = Diode [package=diode-1n4148]
  D4 = Diode [package=diode-1n4148]
  D5 = Diode [package=diode-1n4001]
  R1 = Resistor [tolerance=±5% resistance=4.7k package=THT]
  Onderdeel2 = DR4018
  Switch3 = Switch
  Switch4 = Switch
  Sein5 = Sein3
  Sein6 = Sein3
  Sein7 = Sein3

nets:
  N1: Track1.LEFT, Track1.RIGHT, DR1.1, DR1.2
  N2: Track1.MIDDLE, D1.C, D3.A, R1.Pin_0, Onderdeel2.SIGNAL#44
  N3: Track1.COMMON, DR2.TRACKOUTPUT#5, Onderdeel2.SIGNAL#43
  N4: DR1.COMMON, DR2.TRACKOUTPUT#4, D4.C, D5.A, R1.Pin_1
  N5: DR1.LOCONET, DR2.LocoNetT
  N6: D1.A, D5.C
  N7: D3.C, D4.A
  N8: Onderdeel2.1, Onderdeel2.C#15, Switch3.STRAIGHT, Switch3.COMMON
  N9: Onderdeel2.2, Switch3.THROWN
  N10: Onderdeel2.3, Onderdeel2.C#18, Onderdeel2.4, Onderdeel2.5, Onderdeel2.7, Switch4.STRAIGHT, Switch4.THROWN, Switch4.COMMON, Sein7.RED, Sein7.GREEN
  N11: Onderdeel2.C#21, Sein7.COMMON
  N12: Onderdeel2.6, Sein7.YELLOW
  N13: Onderdeel2.9, Onderdeel2.11, Sein6.RED, Sein6.GREEN
  N14: Onderdeel2.C#30, Sein6.COMMON
  N15: Onderdeel2.10, Sein6.YELLOW
  N16: Onderdeel2.13, Onderdeel2.15, Sein5.RED, Sein5.GREEN
  N17: Onderdeel2.C#36, Sein5.COMMON
  N18: Onderdeel2.14, Sein5.YELLOW

notes:
  Loconet cable
